# Fritzing sketch winding design (saved by Fritzing 0.9.3b)
breadboards: 1

parts:
  Part1 = Arduino Mega 2560 (Rev3)
  start = Pushbutton [package="[THT]"]
  R3 = Resistor [tolerance=±5% resistance=220 package="0402 [SMD]"]
  Sensor_5 = FC-03 [chip_label=FC-03]
  Sensor_4 = FC-03 [chip_label=FC-03]
  Sensor_3 = FC-03 [chip_label=FC-03]
  Sensor_2 = FC-03 [chip_label=FC-03]
  Sensor_1 = FC-03 [chip_label=FC-03]
  Cable_Meter = FC-03 [chip_label=FC-03]
  15/20 = Toggle Switch [package=THT]
  Stop = Pushbutton [package="[THT]"]
  R4 = Resistor [tolerance=±5% resistance=220 package="0402 [SMD]"]
  Rever = Pushbutton [package="[THT]"]
  R5 = Resistor [tolerance=±5% resistance=220 package="0402 [SMD]"]
  A/M = Toggle Switch [package=THT]
  A1 = 2 channel relay module [package=THT]
  R6 = Resistor [tolerance=±5% resistance=220 package="0402 [SMD]"]
  R7 = Resistor [tolerance=±5% resistance=220 package="0402 [SMD]"]
  R8 = Resistor [tolerance=±5% resistance=220 package="0402 [SMD]"]
  R9 = Resistor [tolerance=±5% resistance=220 package="0402 [SMD]"]
  S1 = H-Bridge with L298N

nets:
  GND: Part1.GND, R3.Pin_1, Sensor_5.pin_2, Sensor_4.pin_2, Sensor_3.pin_2, Sensor_2.pin_2, Sensor_1.pin_2, Cable_Meter.pin_2, 15/20.COM, R4.Pin_1, R5.Pin_1, A/M.COM, A1.pin_14, S1.GND
  N1: Part1.D13_PWM, A/M.L1, R9.Pin_0
  N2: Part1.D12_PWM, A/M.L2, R8.Pin_0
  N3: Part1.D11_PWM, 15/20.L1, R7.Pin_0
  N4: Part1.D10_PWM, 15/20.L2, R6.Pin_0
  N5: Part1.D9_PWM, Rever.Pin_3, Rever.Pin_4, R5.Pin_0
  N6: Part1.D8_PWM, Stop.Pin_3, Stop.Pin_4, R4.Pin_0
  N7: Part1.3V3, start.Pin_1, start.Pin_2, Sensor_5.pin_1, Sensor_4.pin_1, Sensor_3.pin_1, Sensor_2.pin_1, Sensor_1.pin_1, Cable_Meter.pin_1, Stop.Pin_1, Stop.Pin_2, Rever.Pin_1, Rever.Pin_2, R6.Pin_1, R7.Pin_1, R8.Pin_1, R9.Pin_1
  5V: Part1.5V, A1.pin_13, S1.5V
  N8: Part1.D5_PWM, A1.pin_15
  N9: Part1.D6_PWM, A1.pin_16
  N10: Part1.D7_PWM, start.Pin_3, start.Pin_4, R3.Pin_0
  N11: Part1.D22, Cable_Meter.pin_3
  N12: Part1.D24, Sensor_1.pin_3
  N13: Part1.D26, Sensor_2.pin_3
  N14: Part1.D28, Sensor_3.pin_3
  N15: Part1.D30, Sensor_4.pin_3
  N16: Part1.D32, Sensor_5.pin_3
  N17: Part1.D34, S1.IN1
  N18: Part1.D36, S1.IN2

custom parts:
  FC-03: FC-03, LM393 IR Speed Sensor Encoder
  2 channel relay module: 2 channel Relay Module 5V 12V 24V High and Low Level Trigger Relay Control With Optocoupler Two Way relays DC 5 V 12 V 24 V Volt.
  H-Bridge with L298N: h-bridge
